# Fritzing sketch project (saved by Fritzing 0.9.3b)
circuit board: 8.46667cm x 5.64444cm
breadboards: 1

parts:
  Demux = 74HC259N [part_number=74HC259N package="DIP (Dual Inline) [THT]"]
  Latch = 74HC259N [part_number=74HC259N package="DIP (Dual Inline) [THT]"]
  R2 = Resistor [tolerance=±5% resistance=1k package=THT]
  LED1 = LED - 5mm [color="Red (633nm)" package="5 mm [THT]"]
  R1 = Resistor [tolerance=±5% resistance=10k package=THT]
  Part1 = Arduino Micro (Rev3)
  R4 = Resistor [tolerance=±5% resistance=10k package=THT]
  R5 = Resistor [tolerance=±5% resistance=10k package=THT]
  R6 = Resistor [tolerance=±5% resistance=10k package=THT]
  R7 = Resistor [tolerance=±5% resistance=10k package=THT]
  R8 = Resistor [tolerance=±5% resistance=10k package=THT]
  R9 = Resistor [tolerance=±5% resistance=10k package=THT]
  R10 = Resistor [tolerance=±5% resistance=10k package=THT]
  R11 = Resistor [tolerance=±5% resistance=1k package=THT]
  LED2 = LED - 5mm [color="Red (633nm)" package="5 mm [THT]"]
  R12 = Resistor [tolerance=±5% resistance=1k package=THT]
  LED3 = LED - 5mm [color="Red (633nm)" package="5 mm [THT]"]
  R13 = Resistor [tolerance=±5% resistance=1k package=THT]
  LED4 = LED - 5mm [color="Red (633nm)" package="5 mm [THT]"]
  R14 = Resistor [tolerance=±5% resistance=1k package=THT]
  LED5 = LED - 5mm [color="Red (633nm)" package="5 mm [THT]"]
  R15 = Resistor [tolerance=±5% resistance=1k package=THT]
  LED6 = LED - 5mm [color="Red (633nm)" package="5 mm [THT]"]
  R16 = Resistor [tolerance=±5% resistance=1k package=THT]
  LED7 = LED - 5mm [color="Red (633nm)" package="5 mm [THT]"]
  R17 = Resistor [tolerance=±5% resistance=1k package=THT]
  LED8 = LED - 5mm [color="Red (633nm)" package="5 mm [THT]"]
  S1 = Pushbutton [package="[THT]"]
  S2 = Pushbutton [package="[THT]"]
  S3 = Pushbutton [package="[THT]"]
  S4 = Pushbutton [package="[THT]"]
  S5 = Pushbutton [package="[THT]"]
  S6 = Pushbutton [package="[THT]"]
  S7 = Pushbutton [package="[THT]"]
  S8 = Pushbutton [package="[THT]"]

nets:
  N1: Demux.S0, Latch.S0, Part1.D4_PWM/A6
  N2: Demux.S1, Latch.S1, Part1.D5_PWM
  N3: Demux.S2, Latch.S2, Part1.D6_PWM/A7
  N4: Demux.Q0, R1.Pin_0, S1.Pin_3, S1.Pin_4
  N5: Demux.Q1, R4.Pin_0, S2.Pin_3, S2.Pin_4
  N6: Demux.Q2, R5.Pin_0, S3.Pin_3, S3.Pin_4
  N7: Demux.Q3, R6.Pin_0, S4.Pin_3, S4.Pin_4
  GND: Demux.GND, Demux.G_, Demux.CLR_, Latch.GND, R2.Pin_1, R1.Pin_1, Part1.GND, R4.Pin_1, R5.Pin_1, R6.Pin_1, R7.Pin_0, R8.Pin_0, R9.Pin_0, R10.Pin_0, R11.Pin_1, R12.Pin_1, R13.Pin_1, R14.Pin_1, R15.Pin_1, R16.Pin_1, R17.Pin_1
  N8: Demux.Q4, R9.Pin_1, S8.Pin_3, S8.Pin_4
  N9: Demux.Q5, R10.Pin_1, S7.Pin_3, S7.Pin_4
  N10: Demux.Q6, R8.Pin_1, S6.Pin_3, S6.Pin_4
  N11: Demux.Q7, R7.Pin_1, S5.Pin_3, S5.Pin_4
  N12: Demux.Data, Part1.D7
  VCC: Demux.VCC, Latch.CLR_, Latch.VCC, Part1.5V, S1.Pin_1, S1.Pin_2, S2.Pin_1, S2.Pin_2, S3.Pin_1, S3.Pin_2, S4.Pin_1, S4.Pin_2, S5.Pin_1, S5.Pin_2, S6.Pin_1, S6.Pin_2, S7.Pin_1, S7.Pin_2, S8.Pin_1
  N13: Latch.Q0, LED1.anode
  N14: Latch.Q1, LED6.anode
  N15: Latch.Q2, LED2.anode
  N16: Latch.Q3, LED3.anode
  N17: Latch.Q4, LED8.anode
  N18: Latch.Q5, LED7.anode
  N19: Latch.Q6, LED5.anode
  N20: Latch.Q7, LED4.anode
  N21: Latch.Data, Part1.D8_PWM/A8
  N22: Latch.G_, Part1.D9_PWM/A9
  N23: R2.Pin_0, LED1.cathode
  N24: R11.Pin_0, LED2.cathode
  N25: R12.Pin_0, LED3.cathode
  N26: R13.Pin_0, LED4.cathode
  N27: R14.Pin_0, LED5.cathode
  N28: R15.Pin_0, LED6.cathode
  N29: R16.Pin_0, LED7.cathode
  N30: R17.Pin_0, LED8.cathode

custom parts:
  74HC259N: 8-Bit Adressable Latches
