# Fritzing sketch projectv2 (saved by Fritzing 0.9.3b)
circuit board: 20.615cm x 11.2325cm
breadboards: 1

parts:
  JP1 = Header 4 [package=molex-1x4_lock]
  JP2 = Header 4 [package=molex-1x4_lock]
  JP3 = Header 4 [package=molex-1x4_lock]
  JP4 = Header 4 [package=molex-1x4_lock]
  JP5 = Header 4 [package=molex-1x4_lock]
  JP6 = Header 4 [package=molex-1x4_lock]
  JP7 = Header 4 [package=molex-1x4_lock]
  JP8 = Header 4 [package=molex-1x4_lock]
  R1 = Resistor [tolerance=±5% resistance=220 package=THT]
  74HC259N1 = 74HC259N [part_number=74HC259N package="DIP (Dual Inline) [THT]"]
  74HC259N2 = 74HC259N [part_number=74HC259N package="DIP (Dual Inline) [THT]"]
  Part1 = Arduino Micro (Rev3)
  R2 = Resistor [tolerance=±5% resistance=220 package=THT]
  R3 = Resistor [tolerance=±5% resistance=220 package=THT]
  R4 = Resistor [tolerance=±5% resistance=220 package=THT]
  R5 = Resistor [tolerance=±5% resistance=220 package=THT]
  R6 = Resistor [tolerance=±5% resistance=220 package=THT]
  R7 = Resistor [tolerance=±5% resistance=220 package=THT]
  R8 = Resistor [tolerance=±5% resistance=220 package=THT]
  JP9 = Header 3 [package=molex-1x3_lock]
  JP10 = Header 3 [package=molex-1x3_lock]
  JP11 = Header 3 [package=molex-1x3_lock]
  JP12 = Header 3 [package=molex-1x3_lock]
  JP13 = Header 3 [package=molex-1x3_lock]
  JP14 = Header 3 [package=molex-1x3_lock]
  JP16 = Header 2 [package=molex-1x2_lock]
  JP15 = Header 2 [package=molex-1x2_lock]
  C1 = Electrolytic Capacitor [capacitance=1µF package="100 mil [THT, electrolytic]"]

nets:
  VCC: JP1.1, JP2.1, JP3.1, JP4.1, JP5.1, JP6.1, JP7.1, JP8.1, 74HC259N1.CLR_, 74HC259N1.VCC, 74HC259N2.VCC, Part1.5V, JP16.2
  GND: JP1.2, JP2.2, JP3.2, JP4.2, JP5.2, JP6.2, JP7.2, JP8.2, R1.Pin_0, 74HC259N1.GND, 74HC259N2.Q2, 74HC259N2.Q3, 74HC259N2.GND, Part1.GND, R2.Pin_0, R3.Pin_0, R4.Pin_0, R5.Pin_0, R6.Pin_0, R7.Pin_0, R8.Pin_0, JP9.1, JP10.1, JP11.1, JP12.1, JP13.1, JP14.1, JP15.1, C1.-
  N1: JP1.3, 74HC259N1.Q0
  N2: JP1.4, R1.Pin_1, 74HC259N2.Q7
  N3: JP2.3, 74HC259N1.Q1
  N4: JP2.4, 74HC259N2.Data, R2.Pin_1
  N5: JP3.3, 74HC259N1.Q2
  N6: JP3.4, 74HC259N2.G_, R3.Pin_1
  N7: JP4.3, 74HC259N1.Q3
  N8: JP4.4, 74HC259N2.CLR_, R4.Pin_1
  N9: JP5.3, 74HC259N1.Q4
  N10: JP5.4, 74HC259N2.S0, R5.Pin_1
  N11: JP6.3, 74HC259N1.Q5
  N12: JP6.4, 74HC259N2.S1, R6.Pin_1
  N13: JP7.3, 74HC259N1.Q6
  N14: JP7.4, 74HC259N2.Q0, R7.Pin_1
  N15: JP8.3, 74HC259N1.Q7
  N16: JP8.4, 74HC259N2.Q1, R8.Pin_1
  N17: 74HC259N1.S0, Part1.D6_PWM/A7
  N18: 74HC259N1.S1, Part1.D5_PWM
  N19: 74HC259N1.S2, Part1.D4_PWM/A6
  N20: 74HC259N1.Data, Part1.D7
  N21: 74HC259N1.G_, Part1.D8_PWM/A8
  N22: 74HC259N2.S2, Part1.D12_PWM/A11
  N23: 74HC259N2.Q4, Part1.D11_PWM
  N24: 74HC259N2.Q5, Part1.D10_PWM/A10
  N25: 74HC259N2.Q6, Part1.D9_PWM/A9
  N26: Part1.A5, JP9.3
  N27: Part1.A4, JP10.3
  N28: Part1.A3, JP11.3
  N29: Part1.A2, JP12.3
  N30: Part1.A1, JP13.3
  N31: Part1.A0, JP14.3
  N32: JP9.2, JP10.2, JP11.2, JP12.2, JP13.2, JP14.2, JP16.1, JP15.2, C1.+

custom parts:
  74HC259N: 8-Bit Adressable Latches
